# Fritzing sketch desain controll relay (saved by Fritzing 0.9.6b)
circuit board: 8.46667cm x 5.64444cm

parts:
  U1 = 2-Channel 5v Relay Shield [package=relay-2ch5v10a]
  A2 = DORHEA ESP32 GPIO breakout board 30pin
  M2 = DOIT Esp32 DevKit v1 (30 pins long, 11 pins width) [part_number=ESP32S-PIN30]

nets:
  VCC: U1.VCC, A2.Pin_25, A2.Pin_59, A2.Pin_63, A2.Pin_64, A2.Pin_66, M2.3V3
  GND: U1.GND, A2.Pin_1, A2.Pin_2, A2.Pin_5, A2.Pin_6, A2.Pin_7, A2.Pin_8, A2.Pin_9, A2.Pin_10, A2.Pin_11, A2.Pin_12, A2.Pin_13, A2.Pin_27, A2.Pin_28, A2.Pin_29, A2.Pin_30, A2.Pin_31, A2.Pin_32, A2.Pin_33, A2.Pin_34, A2.Pin_35, A2.Pin_36, A2.Pin_37, A2.Pin_38, A2.Pin_39, A2.Pin_40, A2.Pin_41, A2.Pin_42, A2.Pin_43, A2.Pin_44, A2.Pin_45, A2.Pin_46, A2.Pin_47, A2.Pin_48, A2.Pin_49, A2.Pin_50, A2.Pin_51, A2.Pin_52, A2.Pin_53, A2.Pin_58, A2.Pin_67, M2.GND, M2.EN, M2.VP, M2.VN, M2.D34, M2.D35, M2.D32, M2.D33, M2.D25, M2.D26, M2.D27, M2.D14, M2.D12, M2.D13
  N1: U1.IN1, A2.Pin_70, A2.Pin_117, M2.D4
  N2: U1.IN2, A2.Pin_73, A2.Pin_120, M2.D5
  N3: U1.K1-On, U1.K2-In, U1.K2-Off, U1.K2-On
  N4: A2.Pin_54, M2.VIN
  N5: A2.Pin_68, M2.D15
  N6: A2.Pin_69, M2.D2
  N7: A2.Pin_71, M2.RX2
  N8: A2.Pin_72, M2.TX2
  N9: A2.Pin_74, M2.D18
  N10: A2.Pin_75, M2.D19
  N11: A2.Pin_76, A2.Pin_123, M2.D21
  N12: A2.Pin_77, M2.RX0
  N13: A2.Pin_78, M2.TX0
  N14: A2.Pin_79, M2.D22
  N15: A2.Pin_80, M2.D23

notes:
  kabel merah arus listrik utama
  kabel kuning dan orange sebagai controll relay

custom parts:
  2-Channel 5v Relay Shield: 2 Channel 5v Relay Shield w. 2x SPD-06VDC-SD-C
  DORHEA ESP32 GPIO breakout board 30pin: ESP32 shield 30P expansion board, supports two power supply : DC 6.5-16v and USB 5.V
  DOIT Esp32 DevKit v1 (30 pins long, 11 pins width): The DOIT Esp32 DevKit v1 is one of the development board created by DOIT to evaluate the ESP-WROOM-32 module. It is based on the ESP32 microcontroller that boasts Wifi, Bluetooth, Ethernet and Low Power support all in a single chip. (vanepp) made breadboard work, adjusted pin numbering and labels and reduced size of schematic and cleaned up pcb. This chip is 30pins long (2 x15) and 11 pins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
